# Fritzing sketch Sunscreminder (saved by Fritzing 0.8.7b)
breadboards: 1

parts:
  Arduino_Mega_1280 = Arduino Mega 2560 (Rev3)
  UV-Sensor = ML8511 UV Sensor Breakout [part_number=SEN-12705]
  R1 = Resistor [tolerance=±5% resistance=10k package=THT]
  R2 = Resistor [tolerance=±5% resistance=10k package=THT]
  R5 = Resistor [tolerance=±5% resistance=10k package=THT]
  R6 = Resistor [tolerance=±5% resistance=10k package=THT]
  R7 = Resistor [tolerance=±5% resistance=10k package=THT]
  R8 = Resistor [tolerance=±5% resistance=10k package=THT]
  R9 = Resistor [tolerance=±5% resistance=1M package=THT]
  Piezo = Piezo Speaker
  S1 = Pushbutton [package="[THT]"]
  S2 = Pushbutton [package="[THT]"]
  R10 = Resistor [tolerance=±5% resistance=10k package=THT]
  R11 = Resistor [tolerance=±5% resistance=10k package=THT]

nets:
  N1: Arduino_Mega_1280.A12, R6.Pin_0
  N2: Arduino_Mega_1280.A14, UV-Sensor.OUT
  GND: Arduino_Mega_1280.GND, UV-Sensor.GND, R5.Pin_1, R8.Pin_1, R9.Pin_1, Piezo.pin1, R10.Pin_0, R11.Pin_0
  N3: Arduino_Mega_1280.5V, R1.Pin_0, S1.Pin_3, S1.Pin_4, S2.Pin_3, S2.Pin_4
  N4: Arduino_Mega_1280.D31, S1.Pin_1, S1.Pin_2, R10.Pin_1
  N5: Arduino_Mega_1280.D37, S2.Pin_1, S2.Pin_2, R11.Pin_1
  N6: Arduino_Mega_1280.D45, R9.Pin_0, Piezo.pin2
  N7: UV-Sensor.EN, R6.Pin_1, R7.Pin_0
  N8: UV-Sensor.3.3V, R1.Pin_1, R2.Pin_0
  N9: R2.Pin_1, R5.Pin_0
  N10: R7.Pin_1, R8.Pin_0

custom parts:
  ML8511 UV Sensor Breakout: Description: The ML8511 breakout is an easy to use ultraviolet light sensor. The MP8511 UV Sensor works by outputing an analog signal in relation to the amount of UV light it detects. This breakout can be very handy in creating devices that warn the user of sunburn or detect the UV index as it relates to weather conditions. This sensor breakout can detect 280-390nm light most effectively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
